# Fritzing sketch Nodo Sensor V2 (saved by Fritzing 0.9.3b)

parts:
  LoRa_Module1 = Ra-01 - LoRa Module SX1278 [part_number=SX1278]
  Componente1 = Arduino Nano (Rev3.0) (ICSP)
  VCC1 = Battery block 9V
  HC-SR04_Sensor_1 = HC-SR04 Ultrasonic Distance Sensor

nets:
  GND: LoRa_Module1.GND, Componente1.GND, VCC1.-
  N1: LoRa_Module1.NSS, Componente1.D10
  N2: LoRa_Module1.MOSI, Componente1.D11/MOSI
  N3: LoRa_Module1.MISO, Componente1.D12/MISO
  N4: LoRa_Module1.SCK, Componente1.D13/SCK
  3.3V: LoRa_Module1.3.3V, Componente1.3V3
  N5: LoRa_Module1.RESET, Componente1.D9
  N6: LoRa_Module1.DIO0, Componente1.D2
  N7: Componente1.D6, HC-SR04_Sensor_1.TRIG
  N8: Componente1.D7, HC-SR04_Sensor_1.ECHO
  N9: Componente1.VIN, VCC1.+
  5V: Componente1.5V, HC-SR04_Sensor_1.VCC

custom parts:
  Ra-01 - LoRa Module SX1278: The Ra-01 LoRa Module featuring the SX1278 engine by Semtech. Module by AI-Thinker. Module (Ra-01) specifications from: https://www.banggood.com/Ra-01-Smart-Electronics-SX1278-LoRa-Spread-Spectrum-Wireless-Module-Ultra-Far-10KM-433M-p-1130769.html Description: Power supply: DC1.8-3.7V(3.3V) Chip: SX1278 Frequency: 433Mhz Operating temperature: -40~+85°C On Sheild Description (may vary by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
